// Logisim project 8b_cpu_isa2.circ as structural Verilog: 1 circuit, main circuit main
module main (
);

  wire adder_1_cout, adder_2_cout, and_3_out, and_4_out, clock_1_out, d_ff_1_q, d_ff_2_q, d_ff_3_q,
       decoder_1_out0, decoder_1_out1, decoder_1_out2, decoder_1_out3, decoder_1_out4, decoder_1_out5,
       decoder_1_out6, decoder_1_out7, decoder_1_out8, decoder_1_out9, decoder_1_out10, decoder_1_out12,
       decoder_1_out13, decoder_1_out14, decoder_1_out15, decoder_1_out16, decoder_1_out17, decoder_1_out18,
       decoder_1_out26, decoder_1_out27, decoder_1_out28, decoder_1_out29, decoder_1_out30,
       demultiplexer_1_out0, demultiplexer_1_out1, demultiplexer_1_out2, demultiplexer_1_out3,
       demultiplexer_1_out4, demultiplexer_1_out5, demultiplexer_1_out6, demultiplexer_1_out7,
       multiplexer_3_out, multiplexer_4_out, nor_1_out, not_1_out, not_2_out, not_3_out, not_6_out, or_1_out,
       or_2_out, or_3_out, or_4_out, or_5_out, priority_encoder_1_gs, priority_encoder_1_out,
       priority_encoder_2_gs, priority_encoder_3_gs, priority_encoder_3_out, priority_encoder_4_gs,
       priority_encoder_4_out, priority_encoder_5_gs, priority_encoder_6_gs, Reset_out, subtractor_1_bout,
       subtractor_2_bout;
  wire [1:0] priority_encoder_2_out, priority_encoder_6_out;
  wire [2:0] and_1_out, and_2_out, nor_2_out, not_4_out, not_5_out, or_6_out, ProgramROM_data_2, STAT_q;
  wire [3:0] bit_extender_1_out, bit_extender_2_out, priority_encoder_5_out, register_1_q;
  wire [3:3] decoder_1_out31;
  wire [4:0] ProgramROM_data;
  wire [7:0] ACC_q, adder_1_out, adder_2_out, ALU_Output_Reg_q, and_7_out, multiplexer_1_out,
       multiplexer_2_out, multiplexer_5_out, multiplexer_6_out, multiplexer_7_out, or_7_out, PC_q, r0_q,
       r1_q, r2_q, r3_q, r4_q, r5_q, r6_q, r7_q, ram_1_dout, register_2_q, shifter_1_out, shifter_2_out,
       subtractor_1_out, subtractor_2_out, xor_1_out;
  wire [7:3] STAT_q_2;

  Clock clock_1 (.out(clock_1_out));
  not not_1 (not_1_out, d_ff_1_q);
  D_Flip_Flop d_ff_1 (.D(not_1_out), .clk(clock_1_out), .Q(d_ff_1_q), .reset(Reset_out));  // open: Qn, preset
  not not_2 (not_2_out, clock_1_out);
  D_Flip_Flop d_ff_2 (.D(d_ff_1_q), .clk(clock_1_out), .Q(d_ff_2_q), .reset(Reset_out));  // open: Qn, preset
  Decoder #(.select(5)) decoder_1 (
    .out0(decoder_1_out0), .out1(decoder_1_out1), .out2(decoder_1_out2), .out3(decoder_1_out3),
    .out4(decoder_1_out4), .out5(decoder_1_out5), .out6(decoder_1_out6), .out7(decoder_1_out7),
    .out8(decoder_1_out8), .out9(decoder_1_out9), .out10(decoder_1_out10), .out12(decoder_1_out12),
    .out13(decoder_1_out13), .out14(decoder_1_out14), .out15(decoder_1_out15), .out16(decoder_1_out16),
    .out17(decoder_1_out17), .out18(decoder_1_out18), .out26(decoder_1_out26), .out27(decoder_1_out27),
    .out28(decoder_1_out28), .out29(decoder_1_out29), .out30(decoder_1_out30), .out31(decoder_1_out31[3]),
    .sel(ProgramROM_data), .en(d_ff_3_q));  // open: out11, out19, out20, out21, out22, out23, out24, out25
  // Probe on ProgramROM_data
  Button Reset (.out(Reset_out));
  not not_3 (not_3_out, d_ff_3_q);
  D_Flip_Flop d_ff_3 (.D(not_3_out), .clk(not_2_out), .Q(d_ff_3_q), .reset(Reset_out));  // open: Qn, preset
  // Probe on ProgramROM_data_2
  or or_1 (or_1_out, decoder_1_out28, decoder_1_out29);
  ROM ProgramROM (.addr(PC_q), .data({ProgramROM_data, ProgramROM_data_2}));
  Register #(.width(4)) register_1 (
    .D(bit_extender_1_out), .en(or_1_out), .clk(or_1_out), .Q(register_1_q), .clr(Reset_out));
  assign bit_extender_1_out = {{1{decoder_1_out29}}, ProgramROM_data_2};  // Bit_Extender bit_extender_1
  or or_2 (or_2_out, decoder_1_out27, decoder_1_out26);
  assign bit_extender_2_out = {{1{decoder_1_out27}}, ProgramROM_data_2};  // Bit_Extender bit_extender_2
  assign not_4_out = ~{3{register_1_q[3]}};  // NOT_Gate not_4, 3 bits wide
  Multiplexer #(.width(8)) multiplexer_1 (
    .in0(register_2_q), .in1(multiplexer_7_out), .out(multiplexer_1_out), .sel(priority_encoder_1_out));
  Priority_Encoder #(.select(1)) priority_encoder_1 (
    .in0(priority_encoder_5_gs), .in1(decoder_1_out6), .out(priority_encoder_1_out),
    .gs(priority_encoder_1_gs));  // open: en_out, en_in
  Register register_2 (.D({{5{1'b0}}, nor_2_out}), .en(d_ff_2_q), .clk(d_ff_2_q), .Q(register_2_q), .clr(Reset_out));
  // Probe on {ProgramROM_data, ProgramROM_data_2}
  // Probe on priority_encoder_2_out
  Priority_Encoder #(.select(2)) priority_encoder_2 (
    .in0(decoder_1_out1), .in1(decoder_1_out10), .in2(and_3_out), .in3(or_2_out),
    .out(priority_encoder_2_out), .gs(priority_encoder_2_gs));  // open: en_out, en_in
  or or_3 (or_3_out, decoder_1_out15, decoder_1_out17, decoder_1_out7, decoder_1_out8, decoder_1_out12, decoder_1_out13, decoder_1_out14, decoder_1_out16, decoder_1_out18);
  assign and_1_out = register_1_q[2:0] & not_4_out & STAT_q;  // AND_Gate and_1, 3 bits wide
  assign and_2_out = register_1_q[2:0] & {3{register_1_q[3]}} & not_5_out;  // AND_Gate and_2, 3 bits wide
  assign not_5_out = ~STAT_q;  // NOT_Gate not_5, 3 bits wide
  or or_4 (or_4_out, nor_1_out, or_6_out[0], or_6_out[1], or_6_out[2]);
  Register #(.trigger("high")) STAT (
    .D(multiplexer_1_out), .en(priority_encoder_1_gs), .clk(priority_encoder_1_gs), .Q({STAT_q_2, STAT_q}),
    .clr(Reset_out));
  // Probe on nor_2_out[1]
  Multiplexer #(.select(2), .width(8)) multiplexer_2 (
    .in0({{5{1'b0}}, ProgramROM_data_2}), .in1(multiplexer_7_out), .in2(ALU_Output_Reg_q),
    .in3({4'b0000, bit_extender_2_out}), .out(multiplexer_2_out), .sel(priority_encoder_2_out));
  and and_3 (and_3_out, or_3_out, d_ff_2_q);
  and and_4 (and_4_out, or_5_out, or_4_out);
  or or_5 (or_5_out, decoder_1_out31[3], decoder_1_out30);
  nor nor_1 (nor_1_out, register_1_q[0], register_1_q[1], register_1_q[2], register_1_q[3]);
  assign or_6_out = and_1_out | and_2_out;  // OR_Gate or_6, 3 bits wide
  and and_5 (nor_2_out[1], multiplexer_3_out, priority_encoder_3_gs);
  and and_6 (nor_2_out[2], priority_encoder_4_gs, multiplexer_4_out);
  Multiplexer multiplexer_3 (
    .in0(adder_1_cout), .in1(adder_2_cout), .out(multiplexer_3_out), .sel(priority_encoder_3_out));
  Priority_Encoder #(.select(1)) priority_encoder_3 (
    .in0(decoder_1_out17), .in1(decoder_1_out15), .out(priority_encoder_3_out), .gs(priority_encoder_3_gs));  // open: en_out, en_in
  Priority_Encoder #(.select(1)) priority_encoder_4 (
    .in0(decoder_1_out16), .in1(decoder_1_out18), .out(priority_encoder_4_out), .gs(priority_encoder_4_gs));  // open: en_out, en_in
  Multiplexer multiplexer_4 (
    .in0(subtractor_1_bout), .in1(subtractor_2_bout), .out(multiplexer_4_out), .sel(priority_encoder_4_out));
  not not_6 (not_6_out, decoder_1_out0);
  Register #(.trigger("high")) ACC (
    .D(multiplexer_2_out), .en(priority_encoder_2_gs), .clk(priority_encoder_2_gs), .Q(ACC_q), .clr(Reset_out));
  Priority_Encoder #(.select(4)) priority_encoder_5 (
    .in0(decoder_1_out17), .in1(decoder_1_out15), .in2(decoder_1_out7), .in3(decoder_1_out8),
    .in4(decoder_1_out12), .in5(decoder_1_out13), .in6(decoder_1_out14), .in7(decoder_1_out16),
    .in8(decoder_1_out18), .out(priority_encoder_5_out), .gs(priority_encoder_5_gs));  // open: in9, in10, in11, in12, in13, in14, in15, en_out, en_in
  // Probe on priority_encoder_5_out
  Counter #(.trigger("falling")) PC (
    .clr(Reset_out), .load(and_4_out), .up(1'b1), .count(not_6_out), .clk(d_ff_3_q),
    .D({ACC_q[3:0], decoder_1_out31[3], ProgramROM_data_2}), .Q(PC_q));  // open: carry
  // Probe on ACC_q
  Priority_Encoder #(.select(2)) priority_encoder_6 (
    .in0(decoder_1_out9), .in1(decoder_1_out4), .in2(decoder_1_out5), .in3(decoder_1_out2),
    .out(priority_encoder_6_out), .gs(priority_encoder_6_gs));  // open: en_out, en_in
  // Probe on ACC_q
  Adder adder_1 (.a(ACC_q), .b({{5{1'b0}}, ProgramROM_data_2}), .out(adder_1_out), .cin(1'b0), .cout(adder_1_cout));
  Adder adder_2 (.a(ACC_q), .b(multiplexer_7_out), .out(adder_2_out), .cin(1'b0), .cout(adder_2_cout));
  Shifter shifter_1 (.in(ACC_q), .\dist (ProgramROM_data_2), .out(shifter_1_out));
  Shifter #(.shift("lr")) shifter_2 (.in(ACC_q), .\dist (ProgramROM_data_2), .out(shifter_2_out));
  assign or_7_out = ACC_q | multiplexer_7_out;  // OR_Gate or_7, 8 bits wide
  assign and_7_out = ACC_q & multiplexer_7_out;  // AND_Gate and_7, 8 bits wide
  Subtractor subtractor_1 (
    .a(ACC_q), .b(multiplexer_7_out), .out(subtractor_1_out), .bout(subtractor_1_bout));  // open: bin
  Subtractor subtractor_2 (
    .a(ACC_q), .b({{5{1'b0}}, ProgramROM_data_2}), .out(subtractor_2_out), .bout(subtractor_2_bout));  // open: bin
  Multiplexer #(.select(2), .width(8)) multiplexer_5 (
    .in0(ACC_q), .in1(PC_q), .in2({STAT_q_2, STAT_q}), .in3(ram_1_dout), .out(multiplexer_5_out),
    .sel(priority_encoder_6_out));
  Demultiplexer #(.select(3)) demultiplexer_1 (
    .out0(demultiplexer_1_out0), .out1(demultiplexer_1_out1), .out2(demultiplexer_1_out2),
    .out3(demultiplexer_1_out3), .out4(demultiplexer_1_out4), .out5(demultiplexer_1_out5),
    .out6(demultiplexer_1_out6), .out7(demultiplexer_1_out7), .in(priority_encoder_6_gs),
    .sel(ProgramROM_data_2));
  assign xor_1_out = ACC_q ^ multiplexer_7_out;  // XOR_Gate xor_1, 8 bits wide
  // Probe on ACC_q
  // Probe on multiplexer_5_out
  Multiplexer #(.select(4), .width(8)) multiplexer_6 (
    .in0(adder_1_out), .in1(adder_2_out), .in2(shifter_1_out), .in3(shifter_2_out), .in4(or_7_out),
    .in5(and_7_out), .in6(xor_1_out), .in7(subtractor_1_out), .in8(subtractor_2_out),
    .out(multiplexer_6_out), .sel(priority_encoder_5_out));  // open: in9, in10, in11, in12, in13, in14, in15
  RAM #(.trigger("high")) ram_1 (
    .addr(ACC_q), .we(decoder_1_out3), .oe(decoder_1_out2), .din(multiplexer_7_out), .dout(ram_1_dout));
  Register #(.trigger("high")) r0 (
    .D(multiplexer_5_out), .en(demultiplexer_1_out0), .clk(demultiplexer_1_out0), .Q(r0_q), .clr(Reset_out));
  Register #(.trigger("high")) r1 (
    .D(multiplexer_5_out), .en(demultiplexer_1_out1), .clk(demultiplexer_1_out1), .Q(r1_q), .clr(Reset_out));
  Register #(.trigger("high")) r2 (
    .D(multiplexer_5_out), .en(demultiplexer_1_out2), .clk(demultiplexer_1_out2), .Q(r2_q), .clr(Reset_out));
  Register #(.trigger("high")) r3 (
    .D(multiplexer_5_out), .en(demultiplexer_1_out3), .clk(demultiplexer_1_out3), .Q(r3_q), .clr(Reset_out));
  Register #(.trigger("high")) r4 (
    .D(multiplexer_5_out), .en(demultiplexer_1_out4), .clk(demultiplexer_1_out4), .Q(r4_q), .clr(Reset_out));
  Register #(.trigger("high")) r5 (
    .D(multiplexer_5_out), .en(demultiplexer_1_out5), .clk(demultiplexer_1_out5), .Q(r5_q), .clr(Reset_out));
  Register #(.trigger("high")) r6 (
    .D(multiplexer_5_out), .en(demultiplexer_1_out6), .clk(demultiplexer_1_out6), .Q(r6_q), .clr(Reset_out));
  Register #(.trigger("high")) r7 (
    .D(multiplexer_5_out), .en(demultiplexer_1_out7), .clk(demultiplexer_1_out7), .Q(r7_q), .clr(Reset_out));
  Register ALU_Output_Reg (
    .D(multiplexer_6_out), .en(priority_encoder_5_gs), .clk(d_ff_2_q), .Q(ALU_Output_Reg_q), .clr(Reset_out));
  // Probe on ALU_Output_Reg_q
  Multiplexer #(.select(3), .width(8)) multiplexer_7 (
    .in0(r0_q), .in1(r1_q), .in2(r2_q), .in3(r3_q), .in4(r4_q), .in5(r5_q), .in6(r6_q), .in7(r7_q),
    .out(multiplexer_7_out), .sel(ProgramROM_data_2));
  nor nor_2 (nor_2_out[0], multiplexer_6_out[0], multiplexer_6_out[1], multiplexer_6_out[2], multiplexer_6_out[3], multiplexer_6_out[4], multiplexer_6_out[5], multiplexer_6_out[6], multiplexer_6_out[7], ~priority_encoder_5_gs);  // NOR_Gate
  // Probe on ram_1_dout
  // Probe on multiplexer_7_out

  // Notes on the sheet:
  //   Phase-Shifted Clock
  //   HALT
  //   Phase-Shifted Clock
  //   Main Clock
  //   LD
  //   GETPC
  //   GETST
  //   LI
  //   ST
  //   SETST
  //   SHLI
  //   SHRI
  //   SETACC
  //   GETACC
  //   SUB
  //   INC
  //   ADD
  //   XOR
  //   AND
  //   OR
  //   DEC
  //   contents of ProgramROM (hex, n*v repeats v):
  //   8 17 8 77 8 e9 f8 0 9 4e 9 6f 9 e1 fb 57 39 7f 89 4f 56 1f 89 4e 8 e0 fa 57 41 4f 56 1f 89 4e 9 77 a
  //   e1 fa 8 e0 fa
  //   JMPHI
  //   LI0/LI1
endmodule
